# Fritzing sketch PanicBrakeLights (saved by Fritzing 0.9.3b)
breadboards: 1

parts:
  Adafruit_Metro_Mini = Adafruit Metro Mini [part_number="Adafruit #2590"]
  ADXL343_Accelerometer = Adafruit ADXL345 [part_number="Adafruit #1231"]
  Left_Strip = Neopixel Strip -- White (60/m) [part_number=1138]
  Right_Strip = Neopixel Strip -- White (60/m) [part_number=1138]
  LM2596_Buck_Converter = RioRand LM2596
  12V_Motorcycle_Battery = BC9VPC [package=bc9vpc]

nets:
  N1: Adafruit_Metro_Mini.AD5/SCL, ADXL343_Accelerometer.SCL
  N2: Adafruit_Metro_Mini.AD4/SDA, ADXL343_Accelerometer.SDA/SDIO
  N3: Adafruit_Metro_Mini.IO6, Right_Strip.DI
  N4: Adafruit_Metro_Mini.IO5, Left_Strip.DI
  +5V: Adafruit_Metro_Mini.+5V, ADXL343_Accelerometer.VIN
  GND: Adafruit_Metro_Mini.GND, ADXL343_Accelerometer.GND, Left_Strip.GND, Right_Strip.GND, LM2596_Buck_Converter.Pin_4
  +5V_2: Adafruit_Metro_Mini.VIN, Left_Strip.+5V, Right_Strip.+5V, LM2596_Buck_Converter.Pin_3
  N5: LM2596_Buck_Converter.Pin_1, 12V_Motorcycle_Battery.V+
  N6: LM2596_Buck_Converter.Pin_2, 12V_Motorcycle_Battery.V-

notes:
  12V Motorcycle Battery
  Calibrate LB2596 to output 5V
  Left Strip
  Right Strip
  ADXL343 Accelerometer

custom parts:
  Adafruit Metro Mini: We sure love the ATmega328 here at Adafruit, and we use them a lot for our own projects. The processor has plenty of GPIO, Analog inputs, hardware UART SPI and I2C, timers and PWM galore - just enough for most simple projects. When we need to go small, we use a Pro Trinket 3V or 5V, but if you want to have USB-to-Serial built in, we reach for an Adafruit METRO Mini. METRO Mini is the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
  Adafruit ADXL345: Filling out our accelerometer offerings, we now have the really lovely digital ADXL345 from Analog Devices, a triple-axis accelerometer with digital I2C and SPI interface breakout. We added an on-board 3.3V regulator and logic-level shifting circuitry, making it a perfect choice for interfacing with any 3V or 5V microcontroller such as the Arduino. The sensor has three axes of measurements, X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
  Neopixel Strip -- White (60/m): Neopixel Strip, White, 60 pixels per meter.
